// Digital circuit 402101352_CPU.dig as structural Verilog
module _402101352_CPU (
  input  RESET,
  input  DBG_EN,
  input  [2:0] DBG_RSEL,
  input  CLK,
  input  [15:0] DBG_MADDR,
  output [7:0] PC_OUT,
  output [15:0] IR_OUT,
  output [15:0] out_8,
  output [15:0] DBG_ROUT,
  output [15:0] DBG_MOUT
);

  wire A15, ALUSrcA_table, B15, C, C_reg, carry_out, comparator_1_eq, comparator_2_eq, DMEM_str, FlagCapable,
       FlagWrite_final, is_JR, isAddSub, MemWr_table, met_cond, n1, n2, or_2_out, PCSrc_bit0, PCSrc_bit1,
       RegDst_table, RegW_table, same_sign, sign_changed, sub, tmp1, v_raw, we;
  wire [1:0] ALUSrcB, PCSrc_final, WBSel_table;
  wire [2:0] ALUFunc, multiplexer_1_out, Ra, Rw;
  wire [3:0] flag_D_in, Flags_new, FLAGS_OUT;
  wire [7:0] branch_target, D_PC, PC_plus1, PCnext_raw;
  wire [14:0] ALU_A, b_modified;
  wire [15:0] _1D, addsub_result, ALU_B, ALU_Result, and_result, Da, Din, imm4_extended, imm7_extended,
       maskB, or_result, Rs1_Data, shift_result, shl_result, shr_result, xor_result;
  wire [15:15] CTRL_d;

  BitExtender #(.inputBits(4)) imm4 (.in(IR_OUT[3:0]), .out(imm4_extended));
  BitExtender #(.inputBits(7)) imm7 (.in(IR_OUT[6:0]), .out(imm7_extended));
  BitExtender #(.inputBits(10)) offset10 (.in(IR_OUT[9:0]));  // open: out
  Register #(.Bits(8)) PC (.D(D_PC), .C(CLK), .en(1'b1), .Q(PC_OUT));
  Add #(.Bits(8)) add_1 (.a(PC_OUT), .b(8'h1), .c_i(1'b0), .s(PC_plus1));  // open: c_o
  ROM #(.AddrBits(8), .Bits(16), .isProgramMemory("true")) IMEM (.A(PC_OUT), .sel(1'b1), .D(IR_OUT));
  Multiplexer #(.Bits(3)) multiplexer_1 (.sel(DBG_EN), .in_0(IR_OUT[9:7]), .in_1(DBG_RSEL), .out(multiplexer_1_out));
  RegisterFile #(.AddrBits(3), .Bits(16)) registerfile_1 (
    .Din(Din), .we(we), .Rw(Rw), .C(CLK), .Ra(Ra), .Rb(multiplexer_1_out), .Da(Da), .Db(out_8));
  Comparator #(.Bits(3)) comparator_1 (.a(Ra), .b(3'b000), .eq(comparator_1_eq));  // open: gt, lt
  Comparator #(.Bits(3)) comparator_2 (.a(multiplexer_1_out), .b(3'b000), .eq(comparator_2_eq));  // open: gt, lt
  Multiplexer #(.Bits(3)) multiplexer_2 (.sel(1'b0), .in_0(IR_OUT[6:4]), .in_1(IR_OUT[9:7]), .out(Ra));
  Multiplexer #(.Bits(16)) multiplexer_3 (.sel(comparator_1_eq), .in_0(Da), .in_1({16{1'b0}}), .out(Rs1_Data));
  Multiplexer #(.Bits(16)) multiplexer_4 (.sel(comparator_2_eq), .in_0(out_8), .in_1({16{1'b0}}), .out(DBG_ROUT));
  // Probe on comparator_2_eq
  LED led_1 (.in(comparator_2_eq));
  Multiplexer #(.Bits(16)) multiplexer_5 (.sel(ALUSrcA_table), .in_0(Da), .in_1({16{1'b0}}), .out({A15, ALU_A}));
  Multiplexer #(.Bits(16), .Selector_Bits(2)) multiplexer_6 (
    .sel(ALUSrcB), .in_0(out_8), .in_1(imm4_extended), .in_2(imm7_extended), .in_3(DBG_ROUT), .out(ALU_B));
  Multiplexer #(.Bits(16)) multiplexer_7 (.sel(sub), .in_0({16{1'b0}}), .in_1({16{1'b1}}), .out(maskB));
  not not_1 (n1, ALUFunc[1]);
  not not_2 (n2, ALUFunc[2]);
  and and_1 (isAddSub, n1, n2);
  and and_2 (sub, isAddSub, ALUFunc[0]);
  assign {B15, b_modified} = ALU_B ^ maskB;  // XOr xor_1, 16 bits wide
  Add #(.Bits(16)) add_2 (.a({A15, ALU_A}), .b({B15, b_modified}), .c_i(sub), .s(addsub_result), .c_o(carry_out));
  assign and_result = {A15, ALU_A} & ALU_B;  // And and_3, 16 bits wide
  assign or_result = {A15, ALU_A} | ALU_B;  // Or or_1, 16 bits wide
  assign xor_result = {A15, ALU_A} ^ ALU_B;  // XOr xor_2, 16 bits wide
  BarrelShifter #(.Bits(16)) barrelshifter_1 (.in({A15, ALU_A}), .shift({1'b0, ALU_B[3:0]}), .out(shl_result));
  Multiplexer #(.Bits(16), .Selector_Bits(3)) multiplexer_8 (
    .sel(ALUFunc), .in_0(addsub_result), .in_1(addsub_result), .in_2(and_result), .in_3(or_result),
    .in_4(xor_result), .in_5(shift_result), .in_6(shift_result), .in_7(addsub_result), .out(ALU_Result));
  BarrelShifter #(.Bits(16), .direction("right")) barrelshifter_2 (
    .in({A15, ALU_A}), .shift({1'b0, ALU_B[3:0]}), .out(shr_result));
  Comparator #(.Bits(16)) comparator_3 (.a(ALU_Result), .b({16{1'b0}}), .eq(Flags_new[0]));  // open: gt, lt
  and and_4 (C, carry_out, isAddSub);
  Multiplexer #(.Bits(16)) multiplexer_9 (.sel(ALUFunc[0]), .in_0(shl_result), .in_1(shr_result), .out(shift_result));
  xnor xnor_1 (same_sign, A15, B15);
  xor xor_3 (sign_changed, A15, ALU_Result[15]);
  and and_5 (v_raw, sign_changed, same_sign);
  and and_6 (Flags_new[3], isAddSub, v_raw);
  or or_2 (or_2_out, RESET, FlagWrite_final);
  Multiplexer #(.Bits(4)) multiplexer_10 (
    .sel(RESET), .in_0({Flags_new[3], C, ALU_Result[15], Flags_new[0]}), .in_1(4'b0000), .out(flag_D_in));
  Register #(.Bits(4)) register_1 (.D(flag_D_in), .C(CLK), .en(or_2_out), .Q({FLAGS_OUT[3], C_reg, FLAGS_OUT[1:0]}));
  Multiplexer #(.Selector_Bits(2)) multiplexer_11 (
    .sel(IR_OUT[15:14]), .in_0(1'b1), .in_1(FLAGS_OUT[0]), .in_2(FLAGS_OUT[1]), .in_3(FLAGS_OUT[3]),
    .out(met_cond));
  RAMDualAccess #(.AddrBits(16), .Bits(16)) DMEM (
    .str(DMEM_str), .C(CLK), .ld(1'b1), .A1(ALU_Result), .Din1(out_8), .A2(DBG_MADDR), .D1(_1D), .D2(DBG_MOUT));
  ROM #(.AddrBits(4), .Bits(16)) CTRL (
    .A(IR_OUT[13:10]), .sel(1'b1),
    .D({CTRL_d[15], is_JR, FlagCapable, PCSrc_bit1, PCSrc_bit0, WBSel_table, ALUFunc, ALUSrcB, ALUSrcA_table, MemWr_table, RegDst_table, RegW_table}));
  Multiplexer #(.Bits(3)) multiplexer_12 (.sel(RegDst_table), .in_0(IR_OUT[9:7]), .in_1(3'b111), .out(Rw));
  Multiplexer #(.Bits(16), .Selector_Bits(2)) multiplexer_13 (
    .sel(WBSel_table), .in_0(ALU_Result), .in_1(_1D), .in_2({IR_OUT[6:0], {9{1'b0}}}),
    .in_3({{8{1'b0}}, PC_plus1}), .out(Din));
  and and_7 (we, RegW_table, met_cond);
  and and_8 (DMEM_str, MemWr_table, met_cond);
  and and_9 (tmp1, met_cond, FlagCapable);
  and and_10 (FlagWrite_final, tmp1, IR_OUT[0]);
  Multiplexer #(.Bits(8), .Selector_Bits(2)) multiplexer_14 (
    .sel(PCSrc_final), .in_0(PC_plus1), .in_1(branch_target), .in_2(branch_target), .in_3(Da[7:0]),
    .out(PCnext_raw));
  Add #(.Bits(8)) add_3 (.a(PC_plus1), .b(IR_OUT[7:0]), .c_i(1'b0), .s(branch_target));  // open: c_o
  Multiplexer #(.Bits(8)) multiplexer_15 (.sel(RESET), .in_0(PCnext_raw), .in_1({8{1'b0}}), .out(D_PC));
  and and_11 (PCSrc_final[0], PCSrc_bit0, met_cond);
  and and_12 (PCSrc_final[1], PCSrc_bit1, met_cond);

  // Other names for the same wires on the sheet: ALUFunc_0 = ALUFunc[0]; ALUFunc_1 = ALUFunc[1];
  //   ALUFunc_2 = ALUFunc[2]; PCSrc_table[1:0] = {PCSrc_bit1, PCSrc_bit0}; ALU_A[15] = A15;
  //   shift_amount[3:0] = ALU_B[3:0]; shift_amount5[3:0] = ALU_B[3:0]; Flags_new[2:1] = {C, ALU_Result[15]};
  //   N = ALU_Result[15]; S15 = ALU_Result[15]; b_modified[15] = B15; jr_target[7:0] = Da[7:0]; Db[15:0] = out_8;
  //   DBG_ROUT_t[15:0] = DBG_MOUT; Z_reg = FLAGS_OUT[0]; N_reg = FLAGS_OUT[1]; FLAGS_OUT[2] = C_reg;
  //   V_reg = FLAGS_OUT[3]; IMEM_OUT[15:0] = IR_OUT; imm4[3:0] = IR_OUT[3:0]; imm7[6:0] = IR_OUT[6:0];
  //   LUI_result[15:9] = IR_OUT[6:0]; offset10[9:0] = IR_OUT[9:0]; offset_low8[7:0] = IR_OUT[7:0]; S_bit = IR_OUT[0];
  //   Rs2_field[2:0] = IR_OUT[3:1]; Rs1_field[2:0] = IR_OUT[6:4]; Rd_field[2:0] = IR_OUT[9:7];
  //   OPCODE[3:0] = IR_OUT[13:10]; CC[1:0] = IR_OUT[15:14]; PC_plus1_ext[7:0] = PC_plus1;
  //   PCSrc_gated_bit0 = PCSrc_final[0]; PCSrc_gated_bit1 = PCSrc_final[1]; V = Flags_new[3]; Z = Flags_new[0]

  // Notes on the sheet:
  //   contents of IMEM (hex, n*v repeats v):
  //   2885,33ff
  //   contents of CTRL (hex, n*v repeats v):
  //   2001,2041,2081,20c1,2101,2141,2181,11,211,14,29,401,800,1603,5800
endmodule
